// Logisim project cpu.circ as structural Verilog: 2 circuits, main circuit main
module main (
  input  [31:0] INSTRUCTION,
  input  CLOCK,
  output [31:0] FETCH_ADDRESS,
  output [31:0] s0_Value,
  output [31:0] s1_Value,
  output [31:0] s2_Value,
  output [31:0] ra_Value,
  output [31:0] sp_Value
);

  wire ALUsrc, and_1_out, and_2_out, beq, bne, equal, jump, MemtoReg, MemWr, RegDst, RegWr;
  wire [3:0] ALUctr;
  wire [4:0] multiplexer_4_out;
  wire [15:0] IMM16;
  wire [25:0] IMM26;
  wire [31:0] adder_1_out, adder_2_out, bit_extender_1_out, bit_extender_2_out, bit_extender_3_out,
       main_1_read_data_1, main_1_read_data_2, main_2_result, main_3_p5, multiplexer_1_out,
       multiplexer_2_out, multiplexer_3_out, multiplexer_5_out, multiplexer_6_out;

  assign bit_extender_1_out = {{16{1'b0}}, IMM16};  // Bit_Extender bit_extender_1
  Adder #(.width(32)) adder_1 (.a(FETCH_ADDRESS), .b(32'h4), .out(adder_1_out));  // open: cin, cout
  Adder #(.width(32)) adder_2 (.a(adder_1_out), .b(bit_extender_1_out), .out(adder_2_out));  // open: cin, cout
  Multiplexer #(.width(32), .enable("false")) multiplexer_1 (
    .in0(adder_1_out), .in1(adder_2_out), .out(multiplexer_1_out), .sel(and_1_out));
  and and_1 (and_1_out, beq, equal);
  Multiplexer #(.width(32), .enable("false")) multiplexer_2 (
    .in0(multiplexer_1_out), .in1(adder_2_out), .out(multiplexer_2_out), .sel(and_2_out));
  and and_2 (and_2_out, bne, ~equal);  // AND_Gate
  assign bit_extender_2_out = {{6{1'b0}}, IMM26};  // Bit_Extender bit_extender_2
  Multiplexer #(.width(32), .enable("false")) multiplexer_3 (
    .in0(multiplexer_2_out), .in1(bit_extender_2_out), .out(multiplexer_3_out), .sel(jump));
  Register #(.width(32)) PC (.D(multiplexer_3_out), .Q(FETCH_ADDRESS), .clk(CLOCK));  // open: en, clr
  Multiplexer #(.width(5)) multiplexer_4 (
    .in0(INSTRUCTION[20:16]), .in1(INSTRUCTION[25:21]), .out(multiplexer_4_out), .sel(RegDst));  // open: en
  regfile_main main_1 (
    .Read_Register_1(INSTRUCTION[15:11]), .Read_Register_2(INSTRUCTION[20:16]),
    .Write_Register(multiplexer_4_out), .Write_Data(multiplexer_6_out), .Write_Enable(RegWr), .Clock(CLOCK),
    .Read_Data_1(main_1_read_data_1), .Read_Data_2(main_1_read_data_2), .s0_Value(s0_Value),
    .s1_Value(s1_Value), .s2_Value(s2_Value), .ra_Value(ra_Value), .sp_Value(sp_Value));
  assign bit_extender_3_out = {{16{1'b0}}, IMM16};  // Bit_Extender bit_extender_3
  Multiplexer #(.width(32), .enable("false")) multiplexer_5 (
    .in0(main_1_read_data_2), .in1(bit_extender_3_out), .out(multiplexer_5_out), .sel(ALUsrc));
  alu_main main_2 (
    .Switch(ALUctr), .X(main_1_read_data_1), .Equal(equal), .Result(main_2_result), .Y(multiplexer_5_out));  // open: Signed_Overflow
  // mem_main main_3: pin names not known; wires that end beside it: main_2_result, main_1_read_data_2, MemWr, CLOCK, main_3_p5
  Multiplexer #(.width(32), .enable("false")) multiplexer_6 (
    .in0(main_2_result), .in1(main_3_p5), .out(multiplexer_6_out), .sel(MemtoReg));

  // Other names for the same wires on the sheet: clk = CLOCK; fetch_addr[31:0] = FETCH_ADDRESS;
  //   RS[4:0] = INSTRUCTION[15:11]; RT[4:0] = INSTRUCTION[20:16]; RD[4:0] = INSTRUCTION[25:21]; ra[31:0] = ra_Value;
  //   s0[31:0] = s0_Value; s1[31:0] = s1_Value; s2[31:0] = s2_Value; sp[31:0] = sp_Value

  // Notes on the sheet:
  //   Output
  //   These are outputs/inputs from run.circ
  //   Inputs
  //   These are DEBUG/TEST outputs from your circuit.
endmodule

module controller_circ (
  input  [31:0] in_1,
  output jump,
  output RegDst,
  output RegWr,
  output ExtOp,
  output ALUsrc,
  output [3:0] ALUctr,
  output MemWr,
  output MemtoReg,
  output beq,
  output bne
);

  wire or_1_out;

  not not_1 (RegDst, or_1_out);
  or or_1 (or_1_out, in_1[26], in_1[27], in_1[28], in_1[29], in_1[30], in_1[31]);
  not not_2 (jump, RegDst);
  not not_3 (ALUsrc, RegDst);
  not not_4 (MemWr, RegDst);
  not not_5 (MemtoReg, RegDst);
  not not_6 (beq, RegDst);
  not not_7 (bne, RegDst);
  Multiplexer #(.select(5), .width(4)) multiplexer_1 (
    .in0(4'b0000), .in2(4'b0001), .in3(4'b0010), .in16(4'b0101), .in17(4'b0110), .in18(4'b0111),
    .in19(4'b1000), .in22(4'b1001), .in23(4'b1010), .in26(4'b1011), .in27(4'b1100), .out(ALUctr),
    .sel({in_1[5], in_1[3:0]}), .en(RegDst));  // open: in1, in4, in5, in6, in7, in8, in9, in10, in11, in12, in13, in14, in15, in20, in21, in24, in25, in28, in29, in30, in31

  assign in_1[20:11] = {in_1[25:21], in_1[25:21]};
  assign RegWr = RegDst;

  // Other names for the same wires on the sheet: funct[5:0] = in_1[5:0];
  //   instruction[31:0] = {in_1[31:21], in_1[25:21], in_1[25:21], in_1[10:0]}; shamt[4:0] = in_1[10:6];
  //   rd[4:0] = in_1[25:21]; opcode[5:0] = in_1[31:26]; R_format = RegDst

  // Notes on the sheet:
  //   R-format = 1 if opcode is 000000
  //   OUTPUTS
  //   for our ISA, the 4 bit of the funct code is always zero so get rid of it to use a 5bit MUX
endmodule
